# Fritzing sketch Wirint (saved by Fritzing 0.8.3b)
circuit board: 9.3cm x 2.2cm
breadboards: 2

parts:
  ATMega328 = atmega168 [package=dip]
  Timer = Resonator [frequency="16 Mhz" package=THT]
  C1 = Electrolytic Capacitor [capacitance=0.1mF package="100 mil [THT, electrolytic]"]
  VReg = Voltage Regulator - 5V [package="TO220 [THT]"]
  C2 = Electrolytic Capacitor [capacitance=10µF package="100 mil [THT, electrolytic]"]
  LED1 = LED - 5mm [color="Blue (430nm)" package="5 mm [THT]"]
  Q1 = NPN-Transistor [package="TO92 [THT]"]
  Motor = DC Motor
  R2 = Trimmer Potentiometer [maximum_resistance=100kΩ package=THT]
  R1 = Rotary Potentiometer (Small) [maximum_resistance=100kΩ]
  R5 = Resistor [tolerance=±5% resistance=100 package=THT]
  R6 = Resistor [tolerance=±5% resistance=100 package=THT]
  R7 = Resistor [tolerance=±5% resistance=100 package=THT]
  R8 = Resistor [tolerance=±5% resistance=100 package=THT]
  R9 = Resistor [tolerance=±5% resistance=100 package=THT]
  R10 = Resistor [tolerance=±5% resistance=100 package=THT]
  LED2 = LED - 5mm [color="Blue (430nm)" package="5 mm [THT]"]
  LED3 = LED - 5mm [color="Blue (430nm)" package="5 mm [THT]"]
  LED4 = LED - 5mm [color="Blue (430nm)" package="5 mm [THT]"]
  LED5 = LED - 5mm [color="Blue (430nm)" package="5 mm [THT]"]
  LED6 = LED - 5mm [color="Blue (430nm)" package="5 mm [THT]"]
  LED7 = LED - 5mm [color="Blue (430nm)" package="5 mm [THT]"]
  LED8 = LED - 5mm [color="Blue (430nm)" package="5 mm [THT]"]
  R1_2 = Resistor [tolerance=±5% resistance=100 package=THT]
  LCD = LCD screen
  R4 = Resistor [tolerance=±5% resistance=100 package=THT]
  Power = Power plug

nets:
  N1: ATMega328.D3_(PWM), Q1.E
  VCC: ATMega328.VCC, ATMega328.AVCC, ATMega328.AREF, VReg.output_voltage, C2.+, LED1.anode, R2.leg1, R1.leg2, LED2.anode, LED3.anode, LED4.anode, LED5.anode, LED6.anode, LED7.anode, LED8.anode, LCD.VDD, LCD.LED+
  GND: ATMega328.GND, Timer.GND, C1.-, VReg.GND, C2.-, Q1.C, R2.leg2, R1.leg1, R5.Pin_1, R6.Pin_1, R7.Pin_1, R8.Pin_1, R9.Pin_1, R10.Pin_1, R1_2.Pin_1, LCD.VSS, LCD.R/W, LCD.LED-, R4.Pin_1, Power.GND
  N2: ATMega328.XLAT1, Timer.pin_1
  N3: ATMega328.XLAT2, Timer.0
  N4: ATMega328.D7, LCD.RS
  N5: ATMega328.D8, LCD.E
  N6: ATMega328.D9_(PWM), LCD.DB4
  N7: ATMega328.D10_(PWM), LCD.DB5
  N8: ATMega328.D11_(PWM), LCD.DB6
  N9: ATMega328.D12, LCD.DB7
  N10: ATMega328.A0, R1.wiper
  N11: C1.+, VReg.input_voltage, Motor.pin_1, Power.VCC
  N12: LED1.cathode, R1_2.Pin_0
  N13: Q1.B, Motor.pin_2
  N14: R2.wiper, LCD.V0
  N15: R5.Pin_0, LED3.cathode
  N16: R6.Pin_0, LED4.cathode
  N17: R7.Pin_0, LED5.cathode
  N18: R8.Pin_0, LED6.cathode
  N19: R9.Pin_0, LED7.cathode
  N20: R10.Pin_0, LED8.cathode
  N21: LED2.cathode, R4.Pin_0

notes:
  Stir Plate
  12/9/2013

custom parts:
  Power plug: power plug
